// Logisim project 1_27_2022.circ as structural Verilog: 1 circuit, main circuit main
module main (
  input  A,
  input  in_2,
  input  A_2,
  input  B,
  input  C,
  input  in_6,
  input  A_3,
  input  B_2,
  input  C_2,
  input  in_10,
  input  in_11,
  input  NOT,
  input  A_A__prime___A_prime,
  input  AND,
  input  AND_2,
  input  in_16,
  input  in_17,
  input  OR,
  input  OR_2,
  input  in_20,
  input  in_21,
  output out_22,
  output out_23,
  output out_24,
  output out_25,
  output out_26,
  output out_27,
  output out_28,
  output out_29,
  output out_30,
  output out_31,
  output out_32,
  output out_33,
  output out_34
);

  wire A_out, A_prime_BC_out, AB_out, AB_prime_C_2_out, AB_prime_C_3_out, AB_prime_C_out, B_out, C_out,
       nand_2_out, nand_3_out, nand_4_out, nor_2_out, nor_3_out, nor_4_out, xor_1_out, xor_2_out;

  and AB (AB_out, A, in_2);
  and and_1 (out_24, in_6, in_2, A);
  nand AB__prime (out_28, in_10, in_11);
  nand nand_1 (out_29, NOT, NOT);
  nand nand_2 (nand_2_out, AND_2, in_16);
  nand nand_3 (nand_3_out, OR, OR);
  nand nand_4 (nand_4_out, in_21, in_21);
  and AB_C (out_22, AB_out, in_6);
  nand nand_5 (out_31, nand_2_out, nand_2_out);
  nand nand_6 (out_33, nand_3_out, nand_4_out);
  not u_A (A_out, A_2);
  not u_B (B_out, B);
  nor nor_1 (out_30, A_A__prime___A_prime, A_A__prime___A_prime);
  nor nor_2 (nor_2_out, AND, AND);
  nor nor_3 (nor_3_out, in_17, in_17);
  nor nor_4 (nor_4_out, OR_2, in_20);
  not u_C (C_out, C);
  nor nor_5 (out_32, nor_2_out, nor_3_out);
  nor nor_6 (out_34, nor_4_out, nor_4_out);
  and A_prime_BC (A_prime_BC_out, A_out, B, C);
  and AB_prime_C (AB_prime_C_out, A_2, B_out, C);
  or or_1 (out_25, A_prime_BC_out, AB_prime_C_out, AB_prime_C_2_out, AB_prime_C_3_out);
  and AB_prime_C_2 (AB_prime_C_2_out, A_2, B, C_out);
  and AB_prime_C_3 (AB_prime_C_3_out, A_2, B, C);
  xor xor_1 (xor_1_out, A_3, B_2);
  xor xor_2 (xor_2_out, B_2, C_2);
  xor xor_3 (out_23, xor_1_out, C_2);
  xor xor_4 (out_26, A_3, xor_2_out);
  ExactlyOne xor_5 (.out(out_27), .in0(A_3), .in1(B_2), .in2(C_2));

  // Notes on the sheet:
  //   (AA)' = (A)' = A'
  //   ((AB)'(AB)')' = ((AB)')' = AB
  //   A+B = (A'B')'  =A+B
  //   NOT
  //   f(a,b,c) = a'bc + ab'c + abc' + abc
  //   Is XOR associative?
  //   (A^B)^C = A^(B^C) != A^B^C
endmodule
