// Logisim project 2-1-2022 busses.circ as structural Verilog: 1 circuit, main circuit main
module main (
  input  [3:0] in_1,
  input  [3:0] in_2,
  input  in_3,
  input  in_4,
  input  in_5,
  input  in_6,
  output [3:0] out_7,
  output out_8,
  output out_9,
  output out_10,
  output out_11,
  output out_12,
  output out_13,
  output out_14
);

  assign out_7 = in_1 & in_2;  // AND_Gate and_1, 4 bits wide
  assign out_12 = in_4 ? in_3 : 1'bz;  // Controlled_Buffer controlled_buffer_1
  assign out_12 = in_6 ? in_5 : 1'bz;  // Controlled_Buffer controlled_buffer_2

  assign out_8 = out_7[3];
  assign out_9 = out_7[2];
  assign out_10 = out_7[1];
  assign out_11 = out_7[0];
  assign out_13 = out_12;
  assign out_14 = out_12;
endmodule
