// Logisim project 2-17-2022 Ripple carry_2c.circ as structural Verilog: 1 circuit, main circuit main
module main (
  input  op,
  input  [3:0] A,
  input  [3:0] B,
  output [3:0] out_4,
  output Cout
);

  wire adder_1_cout, adder_2_cout, adder_3_cout, xor_1_out, xor_2_out, xor_3_out, xor_4_out;

  xor xor_1 (xor_1_out, B[0], op);
  xor xor_2 (xor_2_out, B[1], op);
  xor xor_3 (xor_3_out, B[2], op);
  xor xor_4 (xor_4_out, B[3], op);
  Adder #(.width(1)) adder_1 (.a(A[0]), .b(xor_1_out), .out(out_4[0]), .cin(op), .cout(adder_1_cout));
  Adder #(.width(1)) adder_2 (.a(A[1]), .b(xor_2_out), .out(out_4[1]), .cin(adder_1_cout), .cout(adder_2_cout));
  Adder #(.width(1)) adder_3 (.a(A[2]), .b(xor_3_out), .out(out_4[2]), .cin(adder_2_cout), .cout(adder_3_cout));
  Adder #(.width(1)) adder_4 (.a(A[3]), .b(xor_4_out), .out(out_4[3]), .cin(adder_3_cout), .cout(Cout));

  // Notes on the sheet:
  //   Flip bits
  //   Ripple-Carry Adder 2's Complement Adder
  //   Add 1
endmodule
