// Logisim project 2-17-2022 adders.circ as structural Verilog: 1 circuit, main circuit main
module main (
  input  in_1,
  input  in_2,
  input  A,
  input  B,
  input  Cin,
  output Sum,
  output Cout,
  output Sum_2,
  output Cout_2
);

  wire and_2_out, and_3_out, xor_2_out;

  xor xor_1 (Sum, in_1, in_2);
  and and_1 (Cout, in_1, in_2);
  xor xor_2 (xor_2_out, A, B);
  and and_2 (and_2_out, A, B);
  xor xor_3 (Sum_2, xor_2_out, Cin);
  and and_3 (and_3_out, xor_2_out, Cin);
  xor xor_4 (Cout_2, and_3_out, and_2_out);

  // Notes on the sheet:
  //   Half-adder
  //   Full-adder: A+B+Cin
endmodule
