// Logisim project 2-22-2022 MUXetc.circ as structural Verilog: 3 circuits, main circuit main
module main (
  input  D0,
  input  D1,
  input  D2,
  input  D3,
  input  C1,
  input  C0,
  output Output
);

  wire and_1_out, and_2_out, and_3_out, and_4_out, not_1_out, not_2_out;

  not not_1 (not_1_out, C1);
  not not_2 (not_2_out, C0);
  and and_1 (and_1_out, D0, not_1_out, not_2_out);
  and and_2 (and_2_out, D1, not_1_out, C0);
  and and_3 (and_3_out, D2, C1, not_2_out);
  and and_4 (and_4_out, D3, C1, C0);
  or or_1 (Output, and_1_out, and_2_out, and_3_out, and_4_out);

  // Notes on the sheet:
  //   Input
  //   Control
  //   4 to 1 Multiplexer
endmodule

module MUX_Function (
  input  A,
  input  B,
  output A_OR_B
);

  Multiplexer #(.select(2), .enable("false")) multiplexer_1 (
    .in0(1'b0), .in1(1'b1), .in2(1'b1), .in3(1'b1), .out(A_OR_B), .sel({A, B}));

  // Notes on the sheet:
  //   OR function with 4 to 1 MUX
endmodule

module MUX_F_A__B__C (
  input  A,
  input  B,
  input  C,
  output out_4
);

  wire multiplexer_1_out, not_1_out;
  wire [2:0] undriven;

  not not_1 (not_1_out, C);
  Multiplexer #(.select(3), .enable("false")) multiplexer_1 (
    .in0(1'b0), .in1(1'b0), .in2(1'b0), .in3(1'b1), .in4(1'b0), .in5(1'b1), .in6(1'b1), .in7(1'b0),
    .out(multiplexer_1_out), .sel(undriven));
  Multiplexer #(.select(2), .enable("false")) multiplexer_2 (
    .in0(1'b0), .in1(C), .in2(C), .in3(not_1_out), .out(out_4), .sel({B, A}));

  // Notes on the sheet:
  //   F(A, B, C) = <3, 5, 6>
  //   8 to 1 MUX
  //   4 to 1 MUX
endmodule
