// Logisim project 2-24-2022 TinyALU.circ as structural Verilog: 2 circuits, main circuit main
module main (
  input  [7:0] Operand_A,
  input  [7:0] Operand_B,
  input  Operation,
  input  [7:0] Operand_A_2,
  input  [7:0] Operand_B_2,
  input  [1:0] Operation_2,
  output [7:0] Result,
  output [7:0] Result_2
);

  wire decoder_1_out0, decoder_1_out1, decoder_2_out0, decoder_2_out1, decoder_2_out2, decoder_2_out3;
  wire [7:0] adder_1_out, adder_2_out, divider_1_out, multiplier_1_out, or_1_out, subtractor_1_out;

  Decoder #(.enable("false")) decoder_1 (.out0(decoder_1_out0), .out1(decoder_1_out1), .sel(Operation));
  Adder adder_1 (.a(Operand_A), .b(Operand_B), .out(adder_1_out));  // open: cin, cout
  assign or_1_out = Operand_A | Operand_B;  // OR_Gate or_1, 8 bits wide
  Adder adder_2 (.a(Operand_A_2), .b(Operand_B_2), .out(adder_2_out));  // open: cin, cout
  assign Result_2 = decoder_2_out0 ? adder_2_out : 8'bz;  // Controlled_Buffer controlled_buffer_1
  assign Result_2 = decoder_2_out1 ? subtractor_1_out : 8'bz;  // Controlled_Buffer controlled_buffer_2
  Subtractor subtractor_1 (.a(Operand_A_2), .b(Operand_B_2), .out(subtractor_1_out));  // open: bin, bout
  Multiplier multiplier_1 (.a(Operand_A_2), .b(Operand_B_2), .out(multiplier_1_out));  // open: cin, cout
  Divider divider_1 (.a(Operand_A_2), .b(Operand_B_2), .out(divider_1_out));  // open: upper, rem
  Decoder #(.select(2), .enable("false")) decoder_2 (
    .out0(decoder_2_out0), .out1(decoder_2_out1), .out2(decoder_2_out2), .out3(decoder_2_out3),
    .sel(Operation_2));
  assign Result = decoder_1_out0 ? adder_1_out : 8'bz;  // Controlled_Buffer controlled_buffer_3
  assign Result = decoder_1_out1 ? or_1_out : 8'bz;  // Controlled_Buffer controlled_buffer_4
  assign Result_2 = decoder_2_out2 ? multiplier_1_out : 8'bz;  // Controlled_Buffer controlled_buffer_5
  assign Result_2 = decoder_2_out3 ? divider_1_out : 8'bz;  // Controlled_Buffer controlled_buffer_6

  // Notes on the sheet:
  //   8-bit, 2 function ALU
  //   Addtion, OR
  //   0: ADD, 1: OR
endmodule

module Comparator (
  input  [7:0] Operand_A,
  input  [7:0] Operand_B,
  output A____B,
  output A___B,
  output A___B_2
);

  wire not_1_out, or_1_out;
  wire [6:0] subtractor_1_out;

  Subtractor subtractor_1 (.a(Operand_A), .b(Operand_B), .out({A___B, subtractor_1_out}));  // open: bin, bout
  or or_1 (or_1_out, subtractor_1_out[0], subtractor_1_out[1], subtractor_1_out[2], subtractor_1_out[3], subtractor_1_out[4], subtractor_1_out[5], subtractor_1_out[6], A___B);
  not not_1 (not_1_out, A___B);
  not not_2 (A____B, or_1_out);
  and and_1 (A___B_2, or_1_out, not_1_out);

  // Notes on the sheet:
  //   Comparator: using subtraction
  //   NOT quite
endmodule
