// Logisim project 2-24-2022 decoders.circ as structural Verilog: 4 circuits, main circuit main
module main (
  input  A,
  input  B,
  output _00,
  output _01,
  output _10,
  output _11
);

  wire not_1_out, not_2_out;

  not not_1 (not_1_out, A);
  not not_2 (not_2_out, B);
  and and_1 (_00, not_1_out, not_2_out);
  and and_2 (_01, not_1_out, B);
  and and_3 (_10, A, not_2_out);
  and and_4 (_11, A, B);

  // Notes on the sheet:
  //   2 to 4 decoder
endmodule

module Decoder_w__Enable (
  input  Enable,
  input  A,
  input  B,
  output _00,
  output _01,
  output _10,
  output _11
);

  wire not_1_out, not_2_out;

  not not_1 (not_1_out, A);
  not not_2 (not_2_out, B);
  and and_1 (_00, not_1_out, Enable, not_2_out);
  and and_2 (_01, not_1_out, Enable, B);
  and and_3 (_10, A, Enable, not_2_out);
  and and_4 (_11, A, Enable, B);

  // Notes on the sheet:
  //   2 to 4 decoder w/ enable
endmodule

module DEMUX (
  input  Input,
  input  A,
  input  B,
  output _00,
  output _01,
  output _10,
  output _11
);

  wire not_1_out, not_2_out;

  not not_1 (not_1_out, A);
  not not_2 (not_2_out, B);
  and and_1 (_00, not_1_out, Input, not_2_out);
  and and_2 (_01, not_1_out, Input, B);
  and and_3 (_10, A, Input, not_2_out);
  and and_4 (_11, A, Input, B);

  // Notes on the sheet:
  //   2 to 4 decoder w/ enable also demultiplexer (DEMUX)
endmodule

module Components (
  input  in_1,
  input  in_2,
  input  in_3,
  output out_4,
  output out_5,
  output out_6,
  output out_7
);

  Demultiplexer demultiplexer_1 (.out0(out_4), .out1(out_5), .in(in_1), .sel(in_2), .en(in_3));
  Decoder decoder_1 (.out0(out_6), .out1(out_7), .sel(in_2), .en(in_3));
endmodule
