// Logisim project FlipFlops.circ as structural Verilog: 3 circuits, main circuit main
module main (
  input  S,
  input  R,
  input  S_2,
  input  R_2,
  output Q_prime,
  output Q,
  output Q_prime_2,
  output Q_2
);

  wire and_1_out, and_2_out, CLK_out;

  Clock CLK (.out(CLK_out));
  nor nor_1 (Q_prime, S, Q);
  nor nor_2 (Q, Q_prime, R);
  and and_1 (and_1_out, S_2, CLK_out);
  and and_2 (and_2_out, CLK_out, R_2);
  nor nor_3 (Q_prime_2, and_1_out, Q_2);
  nor nor_4 (Q_2, Q_prime_2, and_2_out);

  // Notes on the sheet:
  //   Set
  //   Reset
  //   Flip-flops: memory
  //   SR Flip flop
  //   Clocked SR
endmodule

module Clocks (
  input  in_1,
  output out_2,
  output glitch,
  output out_4
);

  wire clock_2_out, clock_3_out, not_1_out;

  Clock clock_1 (.out(out_2));
  Clock clock_2 (.out(clock_2_out));
  Clock clock_3 (.out(clock_3_out));
  and and_1 (glitch, clock_2_out, not_1_out);
  not not_1 (not_1_out, clock_2_out);
  assign out_4 = clock_3_out ? in_1 : 1'bz;  // Controlled_Buffer controlled_buffer_1
endmodule

module D_Flip_Flop (
  input  D,
  input  D_2,
  output Q_prime,
  output Q,
  output Q_2,
  output Q_prime_2
);

  wire and_1_out, and_2_out, and_3_out, and_4_out, and_5_out, and_6_out, CLK_2_out, CLK_out, nor_3_out,
       nor_4_out, not_1_out, not_2_out, not_3_out;

  Clock CLK (.out(CLK_out));
  Clock CLK_2 (.out(CLK_2_out));
  not not_1 (not_1_out, D);
  not not_2 (not_2_out, D_2);
  and and_1 (and_1_out, D, CLK_out);
  and and_2 (and_2_out, CLK_out, not_1_out);
  and and_3 (and_3_out, D_2, CLK_2_out);
  and and_4 (and_4_out, CLK_2_out, not_2_out);
  D_Flip_Flop_part d_ff_1 ();  // open: clk, D, Q, Qn, preset, en, reset
  nor nor_1 (Q_prime, and_1_out, Q);
  nor nor_2 (Q, Q_prime, and_2_out);
  nor nor_3 (nor_3_out, and_3_out, nor_4_out);
  nor nor_4 (nor_4_out, nor_3_out, and_4_out);
  not not_3 (not_3_out, CLK_2_out);
  and and_5 (and_5_out, not_3_out, nor_3_out);
  and and_6 (and_6_out, nor_4_out, not_3_out);
  nor nor_5 (Q_2, and_5_out, Q_prime_2);
  nor nor_6 (Q_prime_2, Q_2, and_6_out);

  // Notes on the sheet:
  //   Set
  //   Reset
  //   Set
  //   Reset
  //   Clocked D
  //   Clocked D
  //   Clocked D
endmodule
