// Logisim project HW4_3.circ as structural Verilog: 1 circuit, main circuit main
module main (
  input  A,
  input  B,
  input  C,
  output out_4
);

  wire not_1_out;

  not not_1 (not_1_out, C);
  Multiplexer #(.select(2), .enable("false")) multiplexer_1 (
    .in0(not_1_out), .in1(1'b0), .in2(C), .in3(not_1_out), .out(out_4), .sel({B, A}));
endmodule
