// Logisim project HW4_4.circ as structural Verilog: 1 circuit, main circuit main
module main (
  input  A,
  input  B,
  input  C,
  output out_4
);

  wire decoder_1_out0, decoder_1_out3, decoder_1_out6;

  Decoder #(.select(3), .enable("false")) decoder_1 (
    .out0(decoder_1_out0), .out3(decoder_1_out3), .out6(decoder_1_out6), .sel({A, B, C}));  // open: out1, out2, out4, out5, out7
  or or_1 (out_4, decoder_1_out0, decoder_1_out3, decoder_1_out6);
endmodule
