// Logisim project HW4_5.circ as structural Verilog: 1 circuit, main circuit main
module main (
  input  i0,
  input  i1,
  input  i2,
  input  i3,
  output F1,
  output F0
);

  wire and_1_out, and_2_out, not_1_out, not_2_out, not_3_out;

  not not_1 (not_1_out, i0);
  not not_2 (not_2_out, i2);
  and and_1 (and_1_out, not_1_out, i1);
  and and_2 (and_2_out, not_1_out, not_2_out);
  and and_3 (F1, not_1_out, not_3_out);
  not not_3 (not_3_out, i1);
  or or_1 (F0, and_1_out, and_2_out);
endmodule
