// Logisim project HW5.circ as structural Verilog: 2 circuits, main circuit main
module main (
  input  M,
  input  c2,
  input  c1,
  input  c0,
  output n2,
  output n1,
  output n0
);

  wire decoder_1_out0, decoder_1_out1, decoder_1_out2, decoder_1_out3, decoder_1_out4, decoder_1_out5,
       decoder_1_out6, decoder_1_out8, decoder_1_out9, decoder_1_out10, decoder_1_out11, decoder_1_out13,
       decoder_1_out14, decoder_1_out15;

  Decoder #(.select(4), .enable("false")) decoder_1 (
    .out0(decoder_1_out0), .out1(decoder_1_out1), .out2(decoder_1_out2), .out3(decoder_1_out3),
    .out4(decoder_1_out4), .out5(decoder_1_out5), .out6(decoder_1_out6), .out8(decoder_1_out8),
    .out9(decoder_1_out9), .out10(decoder_1_out10), .out11(decoder_1_out11), .out13(decoder_1_out13),
    .out14(decoder_1_out14), .out15(decoder_1_out15), .sel({M, c2, c1, c0}));  // open: out7, out12
  or or_1 (n2, decoder_1_out3, decoder_1_out4, decoder_1_out5, decoder_1_out6, decoder_1_out10, decoder_1_out13, decoder_1_out14, decoder_1_out15);
  or or_2 (n1, decoder_1_out1, decoder_1_out2, decoder_1_out5, decoder_1_out6, decoder_1_out9, decoder_1_out11, decoder_1_out10, decoder_1_out14);
  or or_3 (n0, decoder_1_out0, decoder_1_out2, decoder_1_out4, decoder_1_out6, decoder_1_out8, decoder_1_out9, decoder_1_out14, decoder_1_out15);
endmodule

module sequential_circuit (
  input  Reset,
  output [2:0] out_2
);

  wire clock_1_out, main_1_n0, main_1_n1, main_1_n2;

  Clock clock_1 (.out(clock_1_out));
  main main_1 (.M(Reset), .c2(out_2[2]), .c1(out_2[1]), .c0(out_2[0]), .n2(main_1_n2), .n1(main_1_n1), .n0(main_1_n0));
  D_Flip_Flop A2 (.clk(clock_1_out), .D(main_1_n2), .Q(out_2[2]));  // open: Qn, preset, en, reset
  D_Flip_Flop d_ff_1 (.clk(clock_1_out), .D(main_1_n1), .Q(out_2[1]));  // open: Qn, preset, en, reset
  D_Flip_Flop d_ff_2 (.clk(clock_1_out), .D(main_1_n0), .Q(out_2[0]));  // open: Qn, preset, en, reset
endmodule
