// Logisim project Memory.circ as structural Verilog: 1 circuit, main circuit main
module main (
  input  [7:0] Address,
  input  Clock,
  input  Load_Store_prime,
  input  [15:0] Data_In,
  output [15:0] Data_Out
);

  wire not_1_out;

  RAM #(.dataWidth(16)) ram_1 (.addr(Address), .data(Data_Out), .clk(Clock), .ld(Load_Store_prime));  // open: sel, clr
  assign Data_Out = not_1_out ? Data_In : 16'bz;  // Controlled_Buffer controlled_buffer_1
  not not_1 (not_1_out, Load_Store_prime);
endmodule
