// Logisim project Mod8_Counter.circ as structural Verilog: 2 circuits, main circuit main
module main (
  input  Reset,
  output [2:0] out_2
);

  wire Clock_out, next_1_n0, next_1_n1, next_1_n2;

  Clock Clock (.out(Clock_out));
  Next next_1 (.R(Reset), .C2(out_2[2]), .C1(out_2[1]), .C0(out_2[0]), .N2(next_1_n2), .N1(next_1_n1), .N0(next_1_n0));
  D_Flip_Flop Q2 (.clk(Clock_out), .D(next_1_n2), .Q(out_2[2]));  // open: Qn, preset, en, reset
  D_Flip_Flop Q1 (.clk(Clock_out), .D(next_1_n1), .Q(out_2[1]));  // open: Qn, preset, en, reset
  D_Flip_Flop Q0 (.clk(Clock_out), .D(next_1_n0), .Q(out_2[0]));  // open: Qn, preset, en, reset
endmodule

module Next (
  input  R,
  input  C2,
  input  C1,
  input  C0,
  output N2,
  output N1,
  output N0
);

  wire decoder_1_out0, decoder_1_out1, decoder_1_out2, decoder_1_out3, decoder_1_out4, decoder_1_out5,
       decoder_1_out6;

  Decoder #(.select(4)) decoder_1 (
    .out0(decoder_1_out0), .out1(decoder_1_out1), .out2(decoder_1_out2), .out3(decoder_1_out3),
    .out4(decoder_1_out4), .out5(decoder_1_out5), .out6(decoder_1_out6), .sel({R, C2, C1, C0}));  // open: out7, out8, out9, out10, out11, out12, out13, out14, out15, en
  or or_1 (N2, decoder_1_out3, decoder_1_out4, decoder_1_out5, decoder_1_out6);
  or or_2 (N1, decoder_1_out1, decoder_1_out2, decoder_1_out5, decoder_1_out6);
  or or_3 (N0, decoder_1_out0, decoder_1_out2, decoder_1_out4, decoder_1_out6);
endmodule
