// Logisim project RegisterFile.circ as structural Verilog: 1 circuit, main circuit main
module main (
  input  Write,
  input  [7:0] Rd,
  input  [1:0] Select_Rd,
  input  [1:0] Select_Rs,
  input  [1:0] Select_Rt,
  output [7:0] Rs,
  output [7:0] Rt
);

  wire and_1_out, and_2_out, and_3_out, and_4_out, decoder_1_out0, decoder_1_out1, decoder_1_out2,
       decoder_1_out3, decoder_2_out0, decoder_2_out1, decoder_2_out2, decoder_2_out3, decoder_3_out0,
       decoder_3_out1, decoder_3_out2, decoder_3_out3;
  wire [7:0] R0_q, R1_q, R2_q, R3_q;

  Decoder #(.select(2), .enable("false")) decoder_1 (
    .out0(decoder_1_out0), .out1(decoder_1_out1), .out2(decoder_1_out2), .out3(decoder_1_out3),
    .sel(Select_Rd));
  Register R0 (.D(Rd), .Q(R0_q), .clk(and_1_out));  // open: en, clr
  and and_1 (and_1_out, decoder_1_out0, Write);
  Register R1 (.D(Rd), .Q(R1_q), .clk(and_2_out));  // open: en, clr
  and and_2 (and_2_out, decoder_1_out1, Write);
  Register R2 (.D(Rd), .Q(R2_q), .clk(and_3_out));  // open: en, clr
  and and_3 (and_3_out, decoder_1_out2, Write);
  Register R3 (.D(Rd), .Q(R3_q), .clk(and_4_out));  // open: en, clr
  and and_4 (and_4_out, decoder_1_out3, Write);
  Decoder #(.select(2), .enable("false")) decoder_2 (
    .out0(decoder_2_out0), .out1(decoder_2_out1), .out2(decoder_2_out2), .out3(decoder_2_out3),
    .sel(Select_Rs));
  assign Rs = decoder_2_out0 ? R0_q : 8'bz;  // Controlled_Buffer controlled_buffer_1
  assign Rs = decoder_2_out1 ? R1_q : 8'bz;  // Controlled_Buffer controlled_buffer_2
  assign Rs = decoder_2_out2 ? R2_q : 8'bz;  // Controlled_Buffer controlled_buffer_3
  assign Rs = decoder_2_out3 ? R3_q : 8'bz;  // Controlled_Buffer controlled_buffer_4
  Decoder #(.select(2), .enable("false")) decoder_3 (
    .out0(decoder_3_out0), .out1(decoder_3_out1), .out2(decoder_3_out2), .out3(decoder_3_out3),
    .sel(Select_Rt));
  assign Rt = decoder_3_out0 ? R0_q : 8'bz;  // Controlled_Buffer controlled_buffer_5
  assign Rt = decoder_3_out1 ? R1_q : 8'bz;  // Controlled_Buffer controlled_buffer_6
  assign Rt = decoder_3_out2 ? R2_q : 8'bz;  // Controlled_Buffer controlled_buffer_7
  assign Rt = decoder_3_out3 ? R3_q : 8'bz;  // Controlled_Buffer controlled_buffer_8

  // Notes on the sheet:
  //   Register File: 4 registers
endmodule
