// Logisim project cs221_HW3.circ as structural Verilog: 1 circuit, main circuit main
module main (
  input  A,
  input  B,
  input  Ctrl,
  input  A_2,
  input  C,
  input  B_2,
  input  A_3,
  input  Ctrl_2,
  input  B_3,
  input  A_4,
  input  B_4,
  input  C_2,
  output out_13,
  output out_14,
  output out_15,
  output out_16,
  output out_17,
  output out_18
);

  wire A_prime_BC_2_out, A_prime_BC_out, AB_prime_C_prime_2_out, AB_prime_C_prime_out, ABC_2_out, ABC_out,
       ABC_prime_2_out, ABC_prime_out, and_1_out, and_2_out, and_3_out, and_4_out, not_1_out, not_2_out,
       not_3_out, not_4_out, not_5_out, not_6_out, not_7_out, not_8_out, not_9_out, not_10_out;

  not not_1 (not_1_out, A_4);
  not not_2 (not_2_out, C);
  assign out_16 = not_3_out ? A_3 : 1'bz;  // Controlled_Buffer controlled_buffer_1
  not not_3 (not_3_out, Ctrl_2);
  assign out_16 = Ctrl_2 ? B_3 : 1'bz;  // Controlled_Buffer controlled_buffer_2
  not not_4 (not_4_out, B_4);
  and and_1 (and_1_out, A_2, not_2_out);
  or or_1 (out_13, and_1_out, and_2_out);
  and and_2 (and_2_out, C, B_2);
  not not_5 (not_5_out, C_2);
  and A_prime_BC (A_prime_BC_out, not_1_out, B_4, C_2);
  and AB_prime_C_prime (AB_prime_C_prime_out, A_4, not_4_out, not_5_out);
  and ABC_prime (ABC_prime_out, A_4, B_4, not_5_out);
  and ABC (ABC_out, A_4, B_4, C_2);
  or or_2 (out_18, A_prime_BC_out, AB_prime_C_prime_out, ABC_prime_out, ABC_out);
  not not_6 (not_6_out, A);
  not not_7 (not_7_out, B);
  not not_8 (not_8_out, Ctrl);
  and and_3 (and_3_out, A, not_9_out);
  not not_9 (not_9_out, Ctrl);
  and and_4 (and_4_out, Ctrl, B);
  assign out_15 = not_10_out ? A : 1'bz;  // Controlled_Buffer controlled_buffer_3
  not not_10 (not_10_out, Ctrl);
  assign out_15 = Ctrl ? B : 1'bz;  // Controlled_Buffer controlled_buffer_4
  and A_prime_BC_2 (A_prime_BC_2_out, not_6_out, B, Ctrl);
  and AB_prime_C_prime_2 (AB_prime_C_prime_2_out, A, not_7_out, not_8_out);
  and ABC_prime_2 (ABC_prime_2_out, A, B, not_8_out);
  and ABC_2 (ABC_2_out, A, B, Ctrl);
  or or_3 (out_14, and_3_out, and_4_out);
  or or_4 (out_17, A_prime_BC_2_out, AB_prime_C_prime_2_out, ABC_prime_2_out, ABC_2_out);

  // Notes on the sheet:
  //   FOR TESTING ONLY
endmodule
