// Logisim project hw4_draft.circ as structural Verilog: 1 circuit, main circuit main
module main (
  input  A,
  input  C,
  input  B
);

  wire and_1_out, and_2_out, and_3_out, and_4_out, and_5_out, and_6_out, and_7_out, and_8_out, not_1_out,
       not_2_out, not_3_out;

  not not_1 (not_1_out, A);
  not not_2 (not_2_out, C);
  not not_3 (not_3_out, B);
  and and_1 (and_1_out, not_3_out, not_2_out, not_1_out);
  and and_2 (and_2_out, B, A, not_2_out);
  and and_3 (and_3_out, not_3_out, A, C);
  and and_4 (and_4_out, B, not_1_out, C);
  // AND_Gate and_5 has open pins: out=and_5_out
  // AND_Gate and_6 has open pins: out=and_6_out
  and and_7 (and_7_out, B, A, not_2_out);
  // AND_Gate and_8 has open pins: out=and_8_out
  // OR_Gate or_1: pin names not known; wires that end beside it: and_3_out, and_4_out, and_5_out
endmodule
