// Logisim project register_4-bit.circ as structural Verilog: 1 circuit, main circuit main
module main (
  input  [3:0] In_from_bus,
  input  Write,
  input  Enable,
  output [3:0] Out_to_Bus
);

  wire and_1_out, Clock_out, Q0_q, Q1_q, Q2_q, Q3_q;

  Clock Clock (.out(Clock_out));
  and and_1 (and_1_out, Clock_out, Write);
  D_Flip_Flop Q3 (.clk(and_1_out), .D(In_from_bus[3]), .Q(Q3_q));  // open: Qn, preset, en, reset
  D_Flip_Flop Q2 (.clk(and_1_out), .D(In_from_bus[2]), .Q(Q2_q));  // open: Qn, preset, en, reset
  assign Out_to_Bus[3] = Enable ? Q3_q : 1'bz;  // Controlled_Buffer controlled_buffer_1
  D_Flip_Flop Q1 (.clk(and_1_out), .D(In_from_bus[1]), .Q(Q1_q));  // open: Qn, preset, en, reset
  assign Out_to_Bus[2] = Enable ? Q2_q : 1'bz;  // Controlled_Buffer controlled_buffer_2
  D_Flip_Flop Q0 (.clk(and_1_out), .D(In_from_bus[0]), .Q(Q0_q));  // open: Qn, preset, en, reset
  assign Out_to_Bus[1] = Enable ? Q1_q : 1'bz;  // Controlled_Buffer controlled_buffer_3
  assign Out_to_Bus[0] = Enable ? Q0_q : 1'bz;  // Controlled_Buffer controlled_buffer_4
endmodule
